# Fritzing sketch KSU 2 - Wiring Diagram (saved by Fritzing 0.9.3b)
circuit board: 27.6629cm x 21.1343cm
breadboards: 2

parts:
  Part1 = Arduino Mega 2560 (Rev3)
  Part2 = Bluetooth HC-05 Macho
  J9 = Basic Force Sensing Resistor (FSR) [package=THT]
  R2 = Resistor [tolerance=±5% resistance=220 package=THT]
  J10 = Basic Servo
  J12 = Basic Servo
  J13 = Basic Servo
  J14 = Basic Servo
  J15 = Basic Servo
  J16 = Basic Servo
  J17 = Basic Servo
  U5 = Mini-360 DC-DC Buck converter [package=THT]
  BATT1 = LiPoly Battery (1300mAh)
  BATT2 = LiPoly Battery (1300mAh)

nets:
  N1: Part1.A6, J9.pin_1, R2.Pin_1
  N2: Part1.D19/RX1, Part2.TXD
  N3: Part1.D18/TX1, Part2.RXD
  5V: Part1.5V, Part2.VCC, J9.pin_0
  GND: Part1.GND, Part2.GND, R2.Pin_0, J10.gnd, J12.gnd, J13.gnd, J14.gnd, J15.gnd, J16.gnd, J17.gnd, U5.OUT-, BATT2.negative
  N4: Part1.VIN, BATT2.positive
  N5: Part1.D29, J10.pulse
  N6: Part1.D31, J14.pulse
  N7: Part1.D33, J12.pulse
  N8: Part1.D35, J13.pulse
  N9: Part1.D49, J17.pulse
  N10: Part1.D51, J15.pulse
  N11: Part1.D53, J16.pulse
  VCC: J10.vcc, J12.vcc, J13.vcc, J14.vcc, J15.vcc, J16.vcc, J17.vcc, U5.OUT+
  N12: U5.IN-, BATT1.negative
  N13: U5.IN+, BATT1.positive

notes:
  Thumb - Pin 35
  MG 90 Servo Motor
  Ring and Middle Finger - Pin 33
  MG 90 Servo Motor
  Pinky Finger - Pin 29
  MG 90 Servo Motor
  Wrist - Up & Down - Pin 51
  MG996R Servo Motor
  Wrist - Left & Right - Pin 53
  MG996R Servo Motor
  Elbow - Pin 49
  DSServo 35kg Servo Motor
  Pointer Finger - Pin 31
  MG 90 Servo Motor
  7.4 V 1200mAh LiPo Battery
  DC - DC Buck Converter
  7.4 V -> 6 V - 3.5 A
  HM 10 Bluetooth Module ->
  (TX to RX1 and RX to TX1)
  FSR01CE Force Sensor -->
  (Connected to A3 with a 10K Resistor and 5V)

custom parts:
  Mini-360 DC-DC Buck converter: Mini-360 DC-DC Buck converter. Tiny buck step down voltage converter, input voltage 4.75 to 23V output 1 to 17V adjustable. Available from ebay and the like.
  LiPoly Battery (1300mAh): Lithium Ion Polymer Battery (1300mAh)
